# Fritzing sketch blink-sensor-sketch (saved by Fritzing 0.9.3b)
breadboards: 1

parts:
  Part1 = Arduino Uno (Rev3) - ICSP
  R1 = Resistor [tolerance=±5% resistance=220 package="0402 [SMD]"]
  LED2 = LEDs [package=led10mm]
  Part2 = SRF05 Ultrasonic Rangefinder  # not connected

nets:
  N1: Part1.GND, LED2.C
  N2: Part1.D2, R1.Pin_1
  N3: R1.Pin_0, LED2.A
