# Fritzing sketch dcmotor (saved by Fritzing 0.9.3b)
breadboards: 1

parts:
  Part1 = Arduino Uno (Rev3)
  R1 = Resistor [tolerance=±5% resistance=220 package=THT]
  D1 = Zener Diode [part_number=1N4732A breakdown_voltage=3.6V package="300 mil [THT]"]
  Q1 = npn-Powertransistor [package="TO220 [THT]"]
  M1 = DC Motor

nets:
  N1: Part1.D9_PWM, R1.Pin_0
  N2: Part1.5V, D1.cathode, M1.pin_2
  N3: Part1.GND, Q1.emitter
  N4: R1.Pin_1, Q1.base
  N5: D1.anode, Q1.collector, M1.pin_1
